// Digital circuit sevensegment.dig as structural Verilog
module sevensegment (
  input  _1,
  input  _2,
  input  _4,
  input  _8
);

  wire _7410_1_pin3, _7410_1_pin5, _7410_1_pin6, _7410_1_pin8, _7410_1_pin12, _7413_1_pin1, _7413_1_pin2,
       _7413_1_pin4, _7413_1_pin5, not_1_out, notconnected_5_out, notconnected_6_out, notconnected_7_out,
       notconnected_8_out, notconnected_9_out, notconnected_10_out, notconnected_11_out, undriven;

  not not_1 (not_1_out, _8);
  _7410 _7410_1 (
    .pin1(1'b1), .pin2(_4), .pin3(_7410_1_pin3), .pin4(1'b1), .pin5(_7410_1_pin5), .pin6(_7410_1_pin6),
    .pin7(1'b0), .pin8(_7410_1_pin8), .pin9(_7410_1_pin5), .pin10(1'b1), .pin11(_4), .pin12(_7410_1_pin12),
    .pin13(_7410_1_pin3), .pin14(1'b1));
  _7413 _7413_1 (
    .pin1(_7413_1_pin1), .pin2(_7413_1_pin2), .pin4(_7413_1_pin4), .pin5(_7413_1_pin5), .pin7(1'b0),
    .pin8(1'b0), .pin9(_7410_1_pin6), .pin10(_7410_1_pin5), .pin11(1'b1), .pin12(_7410_1_pin3), .pin13(_4),
    .pin14(1'b1));  // open: pin3, pin6
  // NotConnected on _7413_1_pin1
  // Not not_2 has open pins: in=_4, out=open
  not not_3 (_7410_1_pin3, _2);
  // NotConnected on _7413_1_pin2
  not not_4 (_7410_1_pin5, _1);
  // NotConnected on _7413_1_pin4
  // NotConnected on _7413_1_pin5
  Seven_Seg seven_seg_1 (
    .a(notconnected_7_out), .b(notconnected_5_out), .c(notconnected_6_out), .d(notconnected_10_out),
    .e(notconnected_9_out), .f(undriven), .g(notconnected_8_out), .dp(notconnected_11_out));
  // NotConnected on notconnected_5_out
  // NotConnected on notconnected_6_out
  // NotConnected on notconnected_7_out
  // NotConnected on notconnected_8_out
  // NotConnected on notconnected_9_out
  // NotConnected on notconnected_10_out
  // NotConnected on notconnected_11_out
endmodule
